# Fritzing sketch CPX_cable_shield (saved by Fritzing 0.9.3b)
circuit board: 5.23684cm x 5.26498cm
breadboards: 1

parts:
  Part1 = Adafruit Circuit Playground Express [part_number="Adafruit #3333"]
  J1 = shrouded pin header, 14 pins [form="♂ (shrouded male)"]

nets:
  N1: Part1.3.3V, J1.pin4, J1.pin14
  N2: Part1.D6_A1, J1.pin10
  N3: Part1.GND, J1.pin1, J1.pin7, J1.pin11
  N4: Part1.D9_A2, J1.pin12
  N5: Part1.D10_A3, J1.pin13
  N6: Part1.D12_A0_SPEAKER, J1.pin9
  N7: Part1.D0_A6_RX, J1.pin5
  N8: Part1.D3_A4_SCL, J1.pin2
  N9: Part1.D2_A5_SDA, J1.pin3
  N10: Part1.D1_A7_TX, J1.pin6
  N11: Part1.VOUT, J1.pin8

custom parts:
  Adafruit Circuit Playground Express: Circuit Playground Express is the next step towards a perfect introduction to electronics and programming. We've taken the original Circuit Playground Classic and made it even better! Not only did we pack even more sensors in, we also made it even easier to program. You can now start your journey with Microsoft MakeCode block-based or Javascript programming. Then, you can use the same board to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
