# Fritzing sketch CPX_proto_shield (saved by Fritzing 0.9.3b)
circuit board: 5.23684cm x 5.26498cm
breadboards: 1

parts:
  Part1 = Adafruit Circuit Playground Express [part_number="Adafruit #3333"]
  J1 = shrouded pin header, 34 pins [form="♂ (shrouded male)"]  # not connected
  J2 = shrouded pin header, 34 pins [form="♂ (shrouded male)"]
  J3 = shrouded pin header, 34 pins [form="♂ (shrouded male)"]
  J4 = shrouded pin header, 34 pins [form="♂ (shrouded male)"]
  J5 = shrouded pin header, 34 pins [form="♂ (shrouded male)"]
  J6 = shrouded pin header, 26 pins [form="♂ (shrouded male)"]  # not connected
  J7 = shrouded pin header, 26 pins [form="♂ (shrouded male)"]  # not connected
  J9 = shrouded pin header, 26 pins [form="♂ (shrouded male)"]
  J8 = shrouded pin header, 26 pins [form="♂ (shrouded male)"]
  J12 = shrouded pin header, 14 pins [form="♂ (shrouded male)"]
  J13 = shrouded pin header, 14 pins [form="♂ (shrouded male)"]
  J14 = shrouded pin header, 10 pins [form="♂ (shrouded male)"]
  J15 = shrouded pin header, 10 pins [form="♂ (shrouded male)"]
  J11 = shrouded pin header, 22 pins [form="♂ (shrouded male)"]  # not connected
  J10 = shrouded pin header, 22 pins [form="♂ (shrouded male)"]  # not connected

nets:
  N1: Part1.3.3V, J3.pin1, J3.pin34, J14.pin2, J14.pin3, J14.pin4
  N2: Part1.D6_A1, J13.pin8
  N3: Part1.GND, J4.pin1, J4.pin17, J4.pin18, J5.pin1, J5.pin17, J5.pin18, J15.pin7, J15.pin8, J15.pin9
  N4: Part1.D9_A2, J13.pin14
  N5: Part1.D10_A3, J9.pin26
  N6: Part1.D12_A0_SPEAKER, J9.pin14
  N7: Part1.D0_A6_RX, J12.pin7
  N8: Part1.D3_A4_SCL, J8.pin1
  N9: Part1.D2_A5_SDA, J12.pin1
  N10: Part1.D1_A7_TX, J8.pin13
  N11: Part1.VOUT, J3.pin17, J3.pin18
  N12: J2.pin1, J2.pin34
  N13: J2.pin17, J2.pin18
  N14: J4.pin34, J5.pin34

custom parts:
  Adafruit Circuit Playground Express: Circuit Playground Express is the next step towards a perfect introduction to electronics and programming. We've taken the original Circuit Playground Classic and made it even better! Not only did we pack even more sensors in, we also made it even easier to program. You can now start your journey with Microsoft MakeCode block-based or Javascript programming. Then, you can use the same board to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
