# Fritzing sketch breadboard_shield (saved by Fritzing 0.9.3b)
circuit board: 5.23684cm x 5.26498cm
breadboards: 1

parts:
  Part1 = Adafruit Circuit Playground Express [part_number="Adafruit #3333"]
  IC1 = Hex Inverter Schmitt Trigger SN74HC14 [package="DIP (Dual Inline)"]

nets:
  3.3V: Part1.3.3V, IC1.2Y, IC1.VCC
  N1: Part1.D6_A1, IC1.5Y
  GND: Part1.GND, IC1.1A, IC1.GND, IC1.5A
  N2: Part1.D9_A2, IC1.6Y
  N3: Part1.D10_A3, IC1.6A
  N4: Part1.D12_A0_SPEAKER, IC1.4A
  N5: Part1.D0_A6_RX, IC1.3A
  N6: Part1.D3_A4_SCL, IC1.1Y
  N7: Part1.D2_A5_SDA, IC1.2A
  N8: Part1.D1_A7_TX, IC1.3Y
  N9: Part1.VOUT, IC1.4Y

custom parts:
  Adafruit Circuit Playground Express: Circuit Playground Express is the next step towards a perfect introduction to electronics and programming. We've taken the original Circuit Playground Classic and made it even better! Not only did we pack even more sensors in, we also made it even easier to program. You can now start your journey with Microsoft MakeCode block-based or Javascript programming. Then, you can use the same board to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
